// Logisim project CPU 4 BIT ASSIGNMENT.circ as structural Verilog: 4 circuits, main circuit Arithematic logic unit
module Arithematic_logic_unit (
  input  SUBTRACT,
  input  [3:0] A,
  input  [3:0] B,
  input  ASB,
  output [3:0] vALU
);

  wire [3:0] adder_1_out, and_1_out, bit_extender_1_out, xor_1_out;

  assign bit_extender_1_out = {{3{SUBTRACT}}, SUBTRACT};  // Bit_Extender bit_extender_1
  assign and_1_out = A & B;  // AND_Gate and_1, 4 bits wide
  assign xor_1_out = B ^ bit_extender_1_out;  // XOR_Gate xor_1, 4 bits wide
  Adder #(.width(4)) adder_1 (.a(A), .b(xor_1_out), .out(adder_1_out), .cin(SUBTRACT));  // open: cout
  Multiplexer #(.width(4), .enable("false")) multiplexer_1 (.in0(and_1_out), .in1(adder_1_out), .out(vALU), .sel(ASB));
endmodule

module cpu (
);

  wire ASB, Clock, Display_Enable, Reset, Subtract, Writing_Enable;
  wire [1:0] Address_A, Address_B, Data_Address, Register_Source_Select;
  wire [3:0] A, ALU_OUTPUT, B, multiplexer_1_out, Opcode;
  wire [3:2] Data;
  wire [7:0] Program_Counter_q;
  wire [7:6] instructions_data;
  wire [11:6] PROM_data;

  Counter Program_Counter (
    .Q(Program_Counter_q), .clk(Clock), .clr(Reset));  // open: load, D, count, carry, preset, down
  Multiplexer #(.select(2), .width(4), .enable("false")) multiplexer_1 (
    .in0({Data, Address_B}), .in1(ALU_OUTPUT), .in2(A), .out(multiplexer_1_out), .sel(Register_Source_Select));  // open: in3
  ROM #(.dataWidth(16), .Select("low")) PROM (
    .addr(Program_Counter_q),
    .data({Opcode, PROM_data[11:10], Data_Address, PROM_data[7:6], Address_A, Data, Address_B}));
  TTY tty_1 (.data({A[2:0], B}), .clk(Clock), .we(Display_Enable), .clr(Reset));
  Registers registers_1 (
    .Data(multiplexer_1_out), .Write_Enable(Writing_Enable), .Data_Address(Data_Address), .Clock(Clock),
    .A(A), .B(B), .Address_A(Address_A), .Address_B(Address_B), .Reset(Reset));
  Arithematic_logic_unit arithematic_logic_unit_1 (.SUBTRACT(Subtract), .A(A), .B(B), .ASB(ASB), .vALU(ALU_OUTPUT));
  Button button_1 (.out(Reset));
  Clock clock_1 (.out(Clock));
  ROM #(.addrWidth(4), .Select("low")) instructions (
    .addr(Opcode),
    .data({instructions_data, Subtract, ASB, Register_Source_Select, Display_Enable, Writing_Enable}));

  // Other names for the same wires on the sheet: Data[1:0] = Address_B

  // Notes on the sheet:
  //   contents of PROM (hex, n*v repeats v):
  //   1000 1101 1203 1303 3023 2320 7331 3024 8*0 3023
  //   contents of instructions (hex, n*v repeats v):
  //   0 1 9 2 5 5 15 35
endmodule

module Registers (
  input  Reset,
  input  [3:0] Data,
  input  Write_Enable,
  input  [1:0] Address_A,
  input  [1:0] Data_Address,
  input  [1:0] Address_B,
  input  Clock,
  output [3:0] A,
  output [3:0] B
);

  wire and_1_out, and_2_out, and_3_out, and_4_out, decoder_1_out0, decoder_1_out1, decoder_1_out2,
       decoder_1_out3;
  wire [3:0] register_1_q, register_2_q, register_3_q, register_4_q;

  Decoder #(.select(2)) decoder_1 (
    .out0(decoder_1_out0), .out1(decoder_1_out1), .out2(decoder_1_out2), .out3(decoder_1_out3),
    .sel(Data_Address));  // open: en
  and and_1 (and_1_out, Write_Enable, decoder_1_out0);
  and and_2 (and_2_out, Write_Enable, decoder_1_out1);
  and and_3 (and_3_out, Write_Enable, decoder_1_out2);
  and and_4 (and_4_out, Write_Enable, decoder_1_out3);
  Register #(.width(4), .Select("low")) register_1 (
    .D(Data), .en(and_1_out), .Q(register_1_q), .clk(Clock), .clr(Reset));
  Register #(.width(4), .Select("low")) register_2 (
    .D(Data), .en(and_2_out), .Q(register_2_q), .clk(Clock), .clr(Reset));
  Register #(.width(4), .Select("low")) register_3 (
    .D(Data), .en(and_3_out), .Q(register_3_q), .clk(Clock), .clr(Reset));
  Register #(.width(4), .Select("low")) register_4 (
    .D(Data), .en(and_4_out), .Q(register_4_q), .clk(Clock), .clr(Reset));
  Multiplexer #(.select(2), .width(4)) multiplexer_1 (
    .in0(register_1_q), .in1(register_2_q), .in2(register_3_q), .in3(register_4_q), .out(A), .sel(Address_A));  // open: en
  Multiplexer #(.select(2), .width(4), .enable("false")) multiplexer_2 (
    .in0(register_1_q), .in1(register_2_q), .in2(register_3_q), .in3(register_4_q), .out(B), .sel(Address_B));
endmodule

module Display_Circuit (
  input  [6:0] Data,
  input  Clock,
  input  Display_Enable,
  input  Clear
);

  TTY tty_1 (.data(Data), .clk(Clock), .we(Display_Enable), .clr(Clear));
endmodule
